// Logisim project 16seg.circ as structural Verilog: 1 circuit, main circuit main
module main (
  input  in_1,
  input  in_2,
  input  in_3,
  input  in_4,
  input  in_5,
  input  in_6,
  input  in_7,
  input  in_8,
  output a1,
  output a2,
  output b,
  output out_12,
  output c,
  output d1,
  output d2,
  output e,
  output f,
  output g1,
  output g2,
  output h,
  output i,
  output j,
  output k,
  output l,
  output m
);
endmodule
